# Fritzing sketch arduino (saved by Fritzing 0.9.5d)
breadboards: 1

parts:
  Componente1 = Arduino Mega 2560 (Rev3)
  R1 = Resistor [tolerance=±5% resistance=1k package="0603 [SMD]"]
  Componente2 = Bluetooth HC-05 Macho
  R2 = Resistor [tolerance=±5% resistance=1k package="0603 [SMD]"]
  R3 = Resistor [tolerance=±5% resistance=1k package="0603 [SMD]"]

nets:
  GND: Componente1.GND, R1.Pin_0, Componente2.GND
  N1: Componente1.D11_PWM, R3.Pin_0
  N2: Componente1.D10_PWM, Componente2.TXD
  5V: Componente1.5V, Componente2.VCC
  N3: R1.Pin_1, R2.Pin_1
  N4: Componente2.RXD, R2.Pin_0, R3.Pin_1
