# Fritzing sketch Carrinho Final - Emulando RX e TX (saved by Fritzing 0.9.5d)
breadboards: 2

parts:
  L298N1 = L298N DC motor driver
  M2 = DC Motor
  M3 = DC Motor
  JACK1 = 2.1mm Barrel Jack with Terminal Block
  Componente1 = Arduino Uno (Rev3) - ICSP
  R1 = Resistor [tolerance=±5% resistance=1k package=THT]
  R2 = Resistor [tolerance=±5% resistance=1k package=THT]
  R3 = Resistor [tolerance=±5% resistance=1k package=THT]
  Componente2 = FC-03 [chip_label=FC-03]
  Componente3 = FC-03 [chip_label=FC-03]
  Componente4 = Bluetooth HC-05 Macho
  VCC1 = 4 x AAA Battery Mount  # not connected
  VCC2 = Battery block 9V  # not connected

nets:
  N1: L298N1.OUT1, M3.pin_2
  N2: L298N1.OUT2, M3.pin_1
  N3: L298N1.OUT3, M2.pin_2
  N4: L298N1.OUT4, M2.pin_1
  N5: L298N1.12V, JACK1.POS
  N6: L298N1.IN1, Componente1.D10_PWM/SS
  N7: L298N1.IN2, Componente1.D9_PWM
  N8: L298N1.IN3, Componente1.D6_PWM
  N9: L298N1.IN4, Componente1.D5_PWM
  N10: Componente1.A0, Componente3.D0
  N11: Componente1.A1, Componente2.D0
  VCC: Componente1.5V, Componente2.VCC, Componente3.VCC, Componente4.VCC
  GND: Componente1.GND, R3.Pin_0, Componente2.GND, Componente3.GND, Componente4.GND
  N12: Componente1.D2, Componente4.TXD
  N13: Componente1.D3_PWM, R2.Pin_1
  N14: R1.Pin_0, R3.Pin_1
  N15: R1.Pin_1, R2.Pin_0, Componente4.RXD

notes:
  O chip é o LM393 as conexoes vão esta trocadas por esse modelo Fritizing se o mais parecido
  Modulo bluetooth HC05, as Conexoes podem esta trocadas na exemplificação do Fritizing
  Caso for o Carrinho 1 Ele vai se Alimentado por uma fonte de Corrente na tomada, caso for o Carrinho 2 Ele vai ter um conjunto de pilhas. Entre 7 a 20V é Seguro utilizar fonte direte, porem é inviavel ja que o cerebro (Arduino) o limite é 5v.
  Existe duas possibilidades no Modulo Blue, Emulação das portas RX e TX. O Codigo de Taun e Gabriel utilizar esse processor. Utilizando a Biblioteca: SoftwareSerial Seguindo o Processo de Emulação RX: 10 Pin TX: 11 Pin(Obs: caso for utilizar o processo de Emulação é importante reduzir a porta RX para 3.3v pode utilizar resistores)
  A maneira de conectar a Bateria é com Plugin. é apenas um Exemplificação

custom parts:
  L298N DC motor driver: 2x DC motor driver with 78M05 positive voltage regulator (7..35 V) L298N: max 46 V, 2 A Set 5 V Enable jumper to enable 5 V regultor (needed for the L298N) and +5 V output at screw terminal or supply external +5 V at screw terminal Set ENA and/or ENB to +5 V to enable motor permanently or supply ENA and/or ENB with PWM signal IN1 and IN2 set rotation directory for motor A (OUT1/OUT2) IN2 and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
  FC-03: FC-03, LM393 IR Speed Sensor Encoder
