# Fritzing sketch Carrinho Final - Emulando RX e TX  Dois Carrinhos (saved by Fritzing 0.9.5d)
breadboards: 6

parts:
  L298N1 = L298N DC motor driver
  M2 = DC Motor
  M3 = DC Motor
  JACK1 = 2.1mm Barrel Jack with Terminal Block
  Componente1 = Arduino Uno (Rev3) - ICSP
  R1 = Resistor [tolerance=±5% resistance=1k package=THT]
  R2 = Resistor [tolerance=±5% resistance=1k package=THT]
  R3 = Resistor [tolerance=±5% resistance=1k package=THT]
  Componente2 = FC-03 [chip_label=FC-03]
  Componente3 = FC-03 [chip_label=FC-03]
  Componente4 = Bluetooth HC-05 Macho
  VCC1 = 4 x AAA Battery Mount  # not connected
  VCC2 = Battery block 9V  # not connected
  Componente5 = FC-03 [chip_label=FC-03]
  Componente6 = FC-03 [chip_label=FC-03]
  Componente7 = Bluetooth HC-05 Macho
  Componente8 = Arduino Uno (Rev3) - ICSP
  L298N2 = L298N DC motor driver
  M4 = DC Motor
  M5 = DC Motor
  R4 = Resistor [tolerance=±5% resistance=1k package=THT]
  R5 = Resistor [tolerance=±5% resistance=1k package=THT]
  R6 = Resistor [tolerance=±5% resistance=1k package=THT]
  VCC3 = 4 x AAA Battery Mount
  Componente9 = Arduino Uno (Rev3) - ICSP
  L298N3 = L298N DC motor driver
  M6 = DC Motor
  M7 = DC Motor
  R7 = Resistor [tolerance=±5% resistance=1k package=THT]
  R8 = Resistor [tolerance=±5% resistance=1k package=THT]
  R9 = Resistor [tolerance=±5% resistance=1k package=THT]
  Componente10 = FC-03 [chip_label=FC-03]
  Componente11 = FC-03 [chip_label=FC-03]
  Componente12 = Bluetooth HC-05 Macho
  VCC4 = 4 x AAA Battery Mount

nets:
  N1: L298N1.OUT1, M3.pin_2
  N2: L298N1.OUT2, M3.pin_1
  N3: L298N1.OUT3, M2.pin_2
  N4: L298N1.OUT4, M2.pin_1
  N5: L298N1.12V, JACK1.POS
  N6: L298N1.IN1, Componente1.D10_PWM/SS
  N7: L298N1.IN2, Componente1.D9_PWM
  N8: L298N1.IN3, Componente1.D6_PWM
  N9: L298N1.IN4, Componente1.D5_PWM
  N10: Componente1.A0, Componente3.D0
  N11: Componente1.A1, Componente2.D0
  VCC: Componente1.5V, Componente2.VCC, Componente3.VCC, Componente4.VCC
  GND: Componente1.GND, R3.Pin_0, Componente2.GND, Componente3.GND, Componente4.GND
  N12: Componente1.D2, Componente4.TXD
  N13: Componente1.D3_PWM, R2.Pin_1
  N14: R1.Pin_0, R3.Pin_1
  N15: R1.Pin_1, R2.Pin_0, Componente4.RXD
  VCC_2: Componente5.VCC, Componente6.VCC, Componente7.VCC, Componente8.5V, L298N2.5V
  GND_2: Componente5.GND, Componente6.GND, Componente8.GND, L298N2.GND, R5.Pin_1, VCC3.-
  N16: Componente5.A0, Componente8.A0
  N17: Componente6.A0, Componente8.A1
  N18: Componente8.D9_PWM, L298N2.IN2
  N19: Componente8.D10_PWM/SS, L298N2.IN1
  N20: Componente8.D5_PWM, L298N2.IN4
  N21: Componente8.D6_PWM, L298N2.IN3
  N22: L298N2.OUT1, M4.pin_2
  N23: L298N2.OUT2, M4.pin_1
  N24: L298N2.OUT3, M5.pin_2
  N25: L298N2.OUT4, M5.pin_1
  N26: R4.Pin_1, R6.Pin_0
  N27: R5.Pin_0, R6.Pin_1
  N28: Componente9.A0, Componente10.A0
  N29: Componente9.A1, Componente11.A0
  N30: Componente9.D9_PWM, L298N3.IN2
  N31: Componente9.D10_PWM/SS, L298N3.IN1
  GND_3: Componente9.GND, L298N3.GND, R7.Pin_1, Componente10.GND, Componente11.GND, VCC4.-
  N32: Componente9.D3_PWM, R9.Pin_0
  N33: Componente9.D5_PWM, L298N3.IN4
  N34: Componente9.D6_PWM, L298N3.IN3
  VCC_3: Componente9.5V, L298N3.5V, Componente10.VCC, Componente11.VCC, Componente12.VCC
  N35: L298N3.OUT1, M6.pin_2
  N36: L298N3.OUT2, M6.pin_1
  N37: L298N3.OUT3, M7.pin_2
  N38: L298N3.OUT4, M7.pin_1
  N39: R7.Pin_0, R8.Pin_1
  N40: R8.Pin_0, R9.Pin_1

notes:
  O chip é o LM393 as conexoes vão esta trocadas por esse modelo Fritizing se o mais parecido
  Modulo bluetooth HC05, as Conexoes podem esta trocadas na exemplificação do Fritizing
  Caso for o Carrinho 1 Ele vai se Alimentado por uma fonte de Corrente na tomada, caso for o Carrinho 2 Ele vai ter um conjunto de pilhas. Entre 7 a 20V é Seguro utilizar fonte direte, porem é inviavel ja que o cerebro (Arduino) o limite é 5v.
  Existe duas possibilidades no Modulo Blue, Emulação das portas RX e TX. O Codigo de Taun e Gabriel utilizar esse processor. Utilizando a Biblioteca: SoftwareSerial Seguindo o Processo de Emulação RX: 10 Pin TX: 11 Pin(Obs: caso for utilizar o processo de Emulação é importante reduzir a porta RX para 3.3v pode utilizar resistores para melhor durabilidade)
  A maneira de conectar a Bateria é com Plugin. é apenas um Exemplificação
  Mapeamento V2
  Primeiro Mapeamento com a coloração de Fio do Carrinho
  E o Segundo com Cores que corresponde ao que se faz de fato
  O RX Não está connectado no primero porque até o momento não foi realizado o modo Escravo e Mestre. Então so usamos TX para envia comandos via Dispositivo Movel ou Serial Monitor.

custom parts:
  L298N DC motor driver: 2x DC motor driver with 78M05 positive voltage regulator (7..35 V) L298N: max 46 V, 2 A Set 5 V Enable jumper to enable 5 V regultor (needed for the L298N) and +5 V output at screw terminal or supply external +5 V at screw terminal Set ENA and/or ENB to +5 V to enable motor permanently or supply ENA and/or ENB with PWM signal IN1 and IN2 set rotation directory for motor A (OUT1/OUT2) IN2 and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
  FC-03: FC-03, LM393 IR Speed Sensor Encoder
