# Fritzing sketch 6v de alimentacao externaa (saved by Fritzing 0.9.5d)
breadboards: 1

parts:
  Componente1 = Arduino Uno (Rev3)
  M2 = DC Motor
  L298N1 = L298N DC motor driver
  M1 = DC Motor
  D2 = Rectifier Diode [part_number=1N4007 package="Melf DO-213 AB [SMD]"]  # not connected
  Componente2 = Lilypad Battery Connect
  VCC1 = Battery
  VCC2 = Battery

nets:
  N1: Componente1.D9_PWM, L298N1.IN3
  N2: Componente1.D10_PWM/SS, L298N1.IN4
  N3: Componente1.D5_PWM, L298N1.IN1
  N4: Componente1.D6_PWM, L298N1.IN2
  GND: Componente1.GND, L298N1.GND, VCC2.-
  N5: M2.pin_1, L298N1.OUT4
  N6: M2.pin_2, L298N1.OUT3
  N7: L298N1.OUT1, M1.pin_2
  N8: L298N1.OUT2, M1.pin_1
  N9: L298N1.12V, VCC1.+
  N10: Componente2.-, VCC2.+
  N11: Componente2.+, VCC1.-

custom parts:
  L298N DC motor driver: 2x DC motor driver with 78M05 positive voltage regulator (7..35 V) L298N: max 46 V, 2 A Set 5 V Enable jumper to enable 5 V regultor (needed for the L298N) and +5 V output at screw terminal or supply external +5 V at screw terminal Set ENA and/or ENB to +5 V to enable motor permanently or supply ENA and/or ENB with PWM signal IN1 and IN2 set rotation directory for motor A (OUT1/OUT2) IN2 and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
