# Fritzing sketch Tensão externa20_46 (saved by Fritzing 0.9.5d)

parts:
  Componente1 = Arduino Uno (Rev3)
  M2 = DC Motor
  L298N1 = L298N DC motor driver
  M1 = DC Motor
  JACK1 = 2.1mm Barrel Jack with Terminal Block

nets:
  N1: Componente1.D9_PWM, L298N1.IN3
  N2: Componente1.D10_PWM/SS, L298N1.IN4
  N3: Componente1.D5_PWM, L298N1.IN1
  N4: Componente1.D6_PWM, L298N1.IN2
  5V: Componente1.5V, L298N1.5V
  N5: Componente1.GND, JACK1.NEG
  N6: M2.pin_1, L298N1.OUT4
  N7: M2.pin_2, L298N1.OUT3
  N8: L298N1.OUT1, M1.pin_2
  N9: L298N1.OUT2, M1.pin_1
  N10: L298N1.12V, JACK1.POS

custom parts:
  L298N DC motor driver: 2x DC motor driver with 78M05 positive voltage regulator (7..35 V) L298N: max 46 V, 2 A Set 5 V Enable jumper to enable 5 V regultor (needed for the L298N) and +5 V output at screw terminal or supply external +5 V at screw terminal Set ENA and/or ENB to +5 V to enable motor permanently or supply ENA and/or ENB with PWM signal IN1 and IN2 set rotation directory for motor A (OUT1/OUT2) IN2 and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
